# Fritzing sketch sketch (saved by Fritzing 0.9.3b)
breadboards: 1

parts:
  Part5 = Micro Lipo Charger
  U1 = LIPO-1000mAh [package=lipo-1000]  # not connected
  Matrix_keypad1 = KEYPAD 4x4  # not connected
  Part2 = Adafruit HUZZAH ESP8266 [part_number="Adafruit #2471"]
  LED1 = smd LED [color="Red (633nm)" package="1206 [SMD]"]

nets:
  N1: Part5.VBAT, Part2.VBAT
  GND: Part5.GND, Part2.GND, LED1.anode

custom parts:
  Micro Lipo Charger: Oh so handy, this little lipo charger is so small and easy to use you can keep it on your desk or mount it easily into any project! Simply plug it via any MicroUSB cable into a USB port and a 3.7V/4.2V lithium polymer or lithium ion rechargeable battery into the JST plug on the other end. There are two LEDs - one red and one green. While charging, the red LED is lit. When the battery is fully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
  KEYPAD 4x4: Matrix keypad 16 buttons, 4 rows x 4 columns
  Adafruit HUZZAH ESP8266: Add Internet to your next project with an adorable, bite-sized WiFi microcontroller, at a price you like! The ESP8266 processor from Espressif is an 80 MHz microcontroller with a full WiFi front-end (both as client and access point) and TCP/IP stack with DNS support as well. While this chip has been very popular, its also been very difficult to use. Most of the low cost modules are not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
